# Fritzing sketch Arduino circuit dirgram (11-03-23) (saved by Fritzing 0.9.8b)
breadboards: 2

parts:
  RFID-Master = Arduino Uno (Rev3) - ICSP
  Screen-Slave = Arduino Uno (Rev3)
  U1 = LCD-16X2 [package=lcd-16x2_noholes]  # not connected
  LCM1602_IIC1 = LCM1602 IIC [part_number="LCM1602 IIC" chip_label="LCM1602 IIC" package="DIP (Dual Inline) [THT]"]
  Part5 = RFID-RC522-v2
  LED1 = LED - 3mm [color="Red (633nm)" current=0.030 package="3 mm [THT]"]  # not connected
  R1 = Resistor [tolerance=±5% power=0.25 resistance=220 package=THT]  # not connected
  Api-Slave = MKR1000 [part_number=Mkr1000]
  S1 = Pushbutton [package="[THT]"]
  R2 = Resistor [tolerance=±5% power=0.25 resistance=220 package=THT]
  Bc547_133 = NPN-Transistor [package="TO92 [THT]"]
  VaskeMaskine = Header 4 [package=molex-1x4_lock]

nets:
  N1: RFID-Master.A4/SDA, Screen-Slave.A4/SDA, LCM1602_IIC1.SDA, Api-Slave.connector56
  N2: RFID-Master.A5/SCL, Screen-Slave.A5/SCL, LCM1602_IIC1.SCL, Api-Slave.connector55
  N3: RFID-Master.ICSP_MOSI, RFID-Master.D11_PWM/MOSI, Part5.MOSI
  N4: RFID-Master.D9_PWM, Part5.RST
  N5: RFID-Master.D10_PWM/SS, Part5.SDA
  N6: RFID-Master.D12/MISO, Part5.MISO
  N7: RFID-Master.D13/SCK, Part5.SCK
  GND: RFID-Master.GND, Part5.GND
  N8: RFID-Master.3V3, Part5.3_3V
  N9: Screen-Slave.D8, Bc547_133.B
  N10: Screen-Slave.D2, S1.Pin_3, S1.Pin_4, R2.Pin_1
  5V: Screen-Slave.5V, LCM1602_IIC1.VCC
  GND_2: Screen-Slave.GND, LCM1602_IIC1.GND
  N11: LCM1602_IIC1.LED_A, LCM1602_IIC1.LED_B
  N12: Api-Slave.connector23, R2.Pin_0, VaskeMaskine.2
  N13: Api-Slave.connector48, S1.Pin_1, S1.Pin_2, Bc547_133.C
  N14: Bc547_133.E, VaskeMaskine.1

custom parts:
  LCM1602 IIC: I2C-Module to use a 1602 or 2004 LCD on with the wire.h libory Serial LCD Modul
  RFID-RC522-v2: A simple China made RFID-RC522 Reader; do check the pin labels, as this is a MFRC522 based clone.
