# Fritzing sketch Arduino circuit dirgram (saved by Fritzing 0.9.8b)
breadboards: 3

parts:
  Part1 = Arduino Uno (Rev3) - ICSP
  Part3 = Arduino Uno (Rev3)
  Part4 = Arduino Mega 2560 (Rev3)
  U1 = LCD-16X2 [package=lcd-16x2_noholes]  # not connected
  LCM1602_IIC1 = LCM1602 IIC [part_number="LCM1602 IIC" chip_label="LCM1602 IIC" package="DIP (Dual Inline) [THT]"]
  Part5 = RFID-RC522-v2
  LED1 = LED - 3mm [color="Red (633nm)" current=0.030 package="3 mm [THT]"]  # not connected
  R1 = Resistor [tolerance=±5% power=0.25 resistance=220 package=THT]  # not connected

nets:
  N1: Part1.A4/SDA, Part3.A4/SDA, Part4.D20/SDA, LCM1602_IIC1.SDA
  N2: Part1.A5/SCL, Part3.A5/SCL, Part4.D21/SCL, LCM1602_IIC1.SCL
  N3: Part1.ICSP_MOSI, Part1.D11_PWM/MOSI, Part5.MOSI
  N4: Part1.D9_PWM, Part5.RST
  N5: Part1.D10_PWM/SS, Part5.SDA
  N6: Part1.D12/MISO, Part5.MISO
  N7: Part1.D13/SCK, Part5.SCK
  GND: Part1.GND, Part5.GND
  N8: Part1.3V3, Part5.3_3V
  5V: Part3.5V, LCM1602_IIC1.VCC
  GND_2: Part3.GND, LCM1602_IIC1.GND
  N9: LCM1602_IIC1.LED_A, LCM1602_IIC1.LED_B

custom parts:
  LCM1602 IIC: I2C-Module to use a 1602 or 2004 LCD on with the wire.h libory Serial LCD Modul
  RFID-RC522-v2: A simple China made RFID-RC522 Reader; do check the pin labels, as this is a MFRC522 based clone.
